// Logisim project NAND_Gate.circ as structural Verilog: 1 circuit, main circuit main
module main (
  input  A,
  input  B,
  input  A_2,
  input  B_2,
  input  A_3,
  input  B_3,
  input  A_4,
  input  B_4,
  output NAND_O,
  output AND_O,
  output OR_O,
  output XOR_O
);

  wire nand_1_out, nand_2_out, nand_3_out, nand_5_out, nand_6_out, nand_7_out;

  nand nand_1 (nand_1_out, A_3, A_3);
  nand nand_2 (nand_2_out, B_3, B_3);
  nand nand_3 (nand_3_out, A_4, B_4);
  nand nand_4 (NAND_O, A, B);
  nand nand_5 (nand_5_out, A_2, B_2);
  nand nand_6 (nand_6_out, A_4, nand_3_out);
  nand nand_7 (nand_7_out, nand_3_out, B_4);
  nand nand_8 (AND_O, nand_5_out, nand_5_out);
  nand nand_9 (OR_O, nand_1_out, nand_2_out);
  nand nand_10 (XOR_O, nand_6_out, nand_7_out);
endmodule
