// Logisim project Register.circ as structural Verilog: 6 circuits, main circuit main
module main (
  input  in_1,
  input  in_2,
  input  [7:0] in_3,
  input  in_4,
  input  in_5,
  output [7:0] out_6,
  output out_7
);

  _8Register u_8register_1 (
    .i(in_3), .s(in_1), .e(in_2), .o(out_6));  // open: o_2, e_2, o_3, e_3, o_4, e_4, i_2, s_2, out_13, out_14, out_15, out_16, out_17, out_18
  _1M u_1m_1 (.i(in_4), .s(in_5), .o(out_7));
endmodule

module _1M (
  input  i,
  input  s,
  output o
);

  wire _1_out, _2_out, _4_out;

  nand _1 (_1_out, i, s);
  nand _2 (_2_out, _1_out, s);
  nand _3 (o, _1_out, _4_out);
  nand _4 (_4_out, o, _2_out);

  // Notes on the sheet:
  //   1 bit Memory
endmodule

module Buffer (
  input  in_1,
  input  in_2,
  output out_3,
  output out_4
);

  wire nand_1_out;

  buf buffer_1 (out_3, in_1);
  nand nand_1 (nand_1_out, in_2, in_2);
  nand nand_2 (out_4, nand_1_out, nand_1_out);
endmodule

module _8M (
  input  [7:0] i,
  input  s,
  output [7:0] o
);

  _1M u_1m_1 (.i(i[0]), .s(s), .o(o[0]));
  _1M u_1m_2 (.i(i[1]), .s(s), .o(o[1]));
  _1M u_1m_3 (.i(i[2]), .s(s), .o(o[2]));
  _1M u_1m_4 (.i(i[3]), .s(s), .o(o[3]));
  _1M u_1m_5 (.i(i[4]), .s(s), .o(o[4]));
  _1M u_1m_6 (.i(i[5]), .s(s), .o(o[5]));
  _1M u_1m_7 (.i(i[6]), .s(s), .o(o[6]));
  _1M u_1m_8 (.i(i[7]), .s(s), .o(o[7]));
endmodule

module _8Register (
  input  e,
  input  [7:0] i,
  input  e_2,
  input  s,
  input  e_3,
  input  e_4,
  input  [7:0] i_2,
  input  s_2,
  output [7:0] o,
  output [7:0] o_2,
  output [7:0] o_3,
  output [7:0] o_4,
  output [7:0] out_13,
  output [7:0] out_14,
  output [7:0] out_15,
  output [7:0] out_16,
  output [7:0] out_17,
  output [7:0] out_18
);

  wire [7:0] n8m_1_o;

  _8M u_8m_1 (.i(i), .s(s), .o(n8m_1_o));
  _8M u_8m_2 (.i(i_2), .s(s_2), .o(out_13));
  Enabler enabler_1 (.i(n8m_1_o), .s(e), .o(o));
  Enabler enabler_2 (.i(n8m_1_o), .s(e_2), .o(o_2));
  Enabler enabler_3 (.i(n8m_1_o), .s(e_3), .o(o_3));
  Enabler enabler_4 (.i(n8m_1_o), .s(e_4), .o(o_4));

  assign out_14 = out_13;
  assign out_15 = out_13;
  assign out_16 = out_13;
  assign out_17 = out_13;
  assign out_18 = out_13;
endmodule

module Enabler (
  input  [7:0] i,
  input  s,
  output [7:0] o
);

  and and_1 (o[0], s, i[0]);
  and and_2 (o[1], s, i[1]);
  and and_3 (o[2], s, i[2]);
  and and_4 (o[3], s, i[3]);
  and and_5 (o[4], s, i[4]);
  and and_6 (o[5], s, i[5]);
  and and_7 (o[6], s, i[6]);
  and and_8 (o[7], s, i[7]);
endmodule
