// Logisim project Multi_inputGate.circ as structural Verilog
module main (
  input  e,
  input  [1:0] in,
  output o1,
  output o2,
  output o3,
  output o4
);

  Decoder #(.select(2)) decoder_1 (.out0(o1), .out1(o2), .out2(o3), .out3(o4), .sel(in), .en(e));
endmodule

module _1M (
  input  i,
  input  s,
  output o
);

  wire _1_out, _2_out, _4_out;

  nand _1 (_1_out, i, s);
  nand _2 (_2_out, _1_out, s);
  nand _3 (o, _1_out, _4_out);
  nand _4 (_4_out, o, _2_out);

  // Notes on the sheet:
  //   1 bit Memory
endmodule

module Buffer (
  input  in_1,
  input  in_2,
  output out_3,
  output out_4
);

  wire nand_1_out;

  buf buffer_1 (out_3, in_1);
  nand nand_1 (nand_1_out, in_2, in_2);
  nand nand_2 (out_4, nand_1_out, nand_1_out);
endmodule

module _8M (
  input  [7:0] i,
  input  s,
  output [7:0] o
);

  _1M u_1m_1 (.i(i[0]), .s(s), .o(o[0]));
  _1M u_1m_2 (.i(i[1]), .s(s), .o(o[1]));
  _1M u_1m_3 (.i(i[2]), .s(s), .o(o[2]));
  _1M u_1m_4 (.i(i[3]), .s(s), .o(o[3]));
  _1M u_1m_5 (.i(i[4]), .s(s), .o(o[4]));
  _1M u_1m_6 (.i(i[5]), .s(s), .o(o[5]));
  _1M u_1m_7 (.i(i[6]), .s(s), .o(o[6]));
  _1M u_1m_8 (.i(i[7]), .s(s), .o(o[7]));
endmodule

module _8Register (
  input  [7:0] i,
  input  s,
  input  e,
  output [7:0] o
);

  wire [7:0] controlled_buffer_1_out, enabler_1_o, n8m_1_o;

  assign controlled_buffer_1_out = s ? i : 8'bz;  // Controlled_Buffer controlled_buffer_1
  _8M u_8m_1 (.i(controlled_buffer_1_out), .s(s), .o(n8m_1_o));
  Enabler enabler_1 (.i(n8m_1_o), .s(e), .o(enabler_1_o));
  assign o = e ? enabler_1_o : 8'bz;  // Controlled_Buffer controlled_buffer_2
endmodule

module Enabler (
  input  [7:0] i,
  input  s,
  output [7:0] o
);

  and and_1 (o[0], s, i[0]);
  and and_2 (o[1], s, i[1]);
  and and_3 (o[2], s, i[2]);
  and and_4 (o[3], s, i[3]);
  and and_5 (o[4], s, i[4]);
  and and_6 (o[5], s, i[5]);
  and and_7 (o[6], s, i[6]);
  and and_8 (o[7], s, i[7]);
endmodule

module R_ctrl (
  input  in_1,
  input  in_2,
  input  in_3,
  input  in_4,
  input  [7:0] in_5,
  input  i,
  input  c,
  output [7:0] out_8,
  output [7:0] out_9,
  output [7:0] out_10,
  output o
);

  wire and_1_out, not_1_out, not_2_out;

  not not_1 (not_1_out, in_4);
  not not_2 (not_2_out, in_3);
  and and_1 (and_1_out, not_1_out, not_2_out);
  assign out_10 = and_1_out ? in_5 : 8'bz;  // Controlled_Buffer in_Buff
  _8Register RA (.i(out_10), .s(in_1), .e(in_3), .o(out_8));
  assign out_10 = in_3 ? out_8 : 8'bz;  // Controlled_Buffer out_BuffA
  assign o = c ? i : 1'bz;  // Controlled_Buffer controlled_buffer_1
  _8Register RB (.i(out_10), .s(in_2), .e(in_4), .o(out_9));
  assign out_10 = in_4 ? out_9 : 8'bz;  // Controlled_Buffer out_BuffB
endmodule

module Muli_input (
  input  in_1,
  input  in_2,
  input  in_3,
  input  in_4,
  input  in_5,
  input  in_6,
  input  in_7,
  input  in_8,
  input  in_9,
  output out_10,
  output out_11,
  output out_12
);

  wire and_1_out, or_1_out;

  and and_1 (and_1_out, in_1, in_2);
  or or_1 (or_1_out, in_7, in_8);
  and and_2 (out_11, and_1_out, in_6);
  or or_2 (out_12, or_1_out, in_9);
  and and_3 (out_10, in_3, in_4, in_5);
endmodule

module _3x8Decorder (
  input  in_1,
  input  in_2,
  input  in_3,
  output out_4,
  output out_5,
  output out_6,
  output out_7,
  output out_8,
  output out_9,
  output out_10,
  output out_11
);

  wire not_1_out, not_2_out, not_3_out;

  not not_1 (not_1_out, in_1);
  not not_2 (not_2_out, in_2);
  not not_3 (not_3_out, in_3);
  and and_1 (out_4, not_1_out, not_2_out, not_3_out);
  and and_2 (out_5, not_1_out, not_2_out, in_3);
  and and_3 (out_6, not_1_out, in_2, not_3_out);
  and and_4 (out_7, not_1_out, in_2, in_3);
  and and_5 (out_8, in_1, not_2_out, not_3_out);
  and and_6 (out_9, in_1, not_2_out, in_3);
  and and_7 (out_10, in_1, in_2, not_3_out);
  and and_8 (out_11, in_1, in_2, in_3);
endmodule

module _8RAM1 (
  input  y,
  input  x,
  input  b_s,
  input  b_e,
  input  [7:0] b_i,
  output [7:0] b_o
);

  wire AND_ad_out, AND_e_out, AND_s_out;
  wire [7:0] controlled_buffer_1_out, n8register_1_o;

  and AND_ad (AND_ad_out, y, x);
  assign controlled_buffer_1_out = AND_ad_out ? b_i : 8'bz;  // Controlled_Buffer controlled_buffer_1
  assign b_o = AND_ad_out ? n8register_1_o : 8'bz;  // Controlled_Buffer controlled_buffer_2
  and AND_s (AND_s_out, AND_ad_out, b_s);
  and AND_e (AND_e_out, AND_ad_out, b_e);
  _8Register u_8register_1 (.i(controlled_buffer_1_out), .s(AND_s_out), .e(AND_e_out), .o(n8register_1_o));
endmodule
