// Logisim project ALU.circ as structural Verilog: 3 circuits, main circuit main
module main (
  input  [7:0] a,
  input  [7:0] b,
  input  ci,
  output co,
  output [7:0] o
);

  Adder8 adder8_1 (.ci(ci), .a(a), .b(b), .o(o), .co(co));
endmodule

module Adder1 (
  input  a,
  input  b,
  input  ci,
  output sum,
  output co
);

  wire co1_out, co2_out, sum1_out;

  xor sum1 (sum1_out, a, b);
  xor sum2 (sum, sum1_out, ci);
  and co2 (co2_out, sum1_out, ci);
  and co1 (co1_out, a, b);
  or or_1 (co, co2_out, co1_out);
endmodule

module Adder8 (
  input  ci,
  input  [7:0] a,
  input  [7:0] b,
  output [7:0] o,
  output co
);

  wire adder1_1_co, adder1_2_co, adder1_3_co, adder1_4_co, adder1_5_co, adder1_6_co, adder1_7_co;

  Adder1 adder1_1 (.a(a[0]), .b(b[0]), .ci(ci), .sum(o[0]), .co(adder1_1_co));
  Adder1 adder1_2 (.a(a[1]), .b(b[1]), .ci(adder1_1_co), .sum(o[1]), .co(adder1_2_co));
  Adder1 adder1_3 (.a(a[2]), .b(b[2]), .ci(adder1_2_co), .sum(o[2]), .co(adder1_3_co));
  Adder1 adder1_4 (.a(a[3]), .b(b[3]), .ci(adder1_3_co), .sum(o[3]), .co(adder1_4_co));
  Adder1 adder1_5 (.a(a[4]), .b(b[4]), .ci(adder1_4_co), .sum(o[4]), .co(adder1_5_co));
  Adder1 adder1_6 (.a(a[5]), .b(b[5]), .ci(adder1_5_co), .sum(o[5]), .co(adder1_6_co));
  Adder1 adder1_7 (.a(a[6]), .b(b[6]), .ci(adder1_6_co), .sum(o[6]), .co(adder1_7_co));
  Adder1 adder1_8 (.a(a[7]), .b(b[7]), .ci(adder1_7_co), .sum(o[7]), .co(co));
endmodule
